# Fritzing sketch lab2_Schematics (saved by Fritzing 0.9.3b)
breadboards: 1

parts:
  TTP223B2 = TTP223B Capacitive Touch Sensor Module
  BAT1 = Battery Holders [package=lipo-1100mAh]
  BAT2 = Battery Holders [package=lipo-1100mAh]
  hc-sr1 = hc-sr04
  U4 = NodeMCU
  M1 = Dagu DGServo 9g (End View) [part_number=RS001B]
  U5 = NodeMCU
  J1 = Piezo Speaker

nets:
  GND: TTP223B2.GND, BAT2.-, hc-sr1.GND, U4.connector13, M1.gnd, U5.connector16
  VCC: TTP223B2.VCC, U4.connector19, M1.vcc
  N1: TTP223B2.SIG, U4.connector2
  N2: BAT1.+, hc-sr1.VCC, U4.connector15
  N3: hc-sr1.Trig, U4.connector7
  N4: hc-sr1.Echo, U4.connector8
  N5: U4.connector11, U5.connector11
  N6: U4.connector12, U5.connector12
  N7: U5.connector10, J1.pin2

notes:
  Used to move back and forth in our music list
  Servo motor- Attached to a stick, that plays our drum
  Ultra Sonic sensor- Modifing the behavior of our Drum (Servo motor)
  MCU1_master in Serial comm between MCU1 and MCU2
  Buzzer, Our second instrument- controlled through Serial Comm
  MCU2_slave in Serial comm between MCU1 and MCU2

custom parts:
  TTP223B Capacitive Touch Sensor Module: The TTP223B capacitive touch sensor module uses the TTP223B IC. The appropriate voltage is approximately 2 to 5.5 volts.
